// Logisim project 231Lab 3.circ as structural Verilog: 7 circuits, main circuit main
module AND (
  input  in_1,
  input  in_2,
  input  in_3,
  input  in_4,
  input  in_5,
  input  in_6,
  input  in_7,
  input  in_8,
  input  in_9,
  output out_10,
  output out_11,
  output out_12
);

  and and_1 (out_10, in_1, in_2, in_3);
  and and_2 (out_11, in_4, in_5, in_6);
  and and_3 (out_12, in_7, in_8, in_9);
  OR or_1 ();  // open: in_1, in_2, in_3, in_4, in_5, in_6, in_7, in_8, in_9, out_10, out_11, out_12
endmodule

module main (
  input  C,
  input  B,
  input  A,
  output out_4
);

  wire and_1_out_10, and_1_out_11, and_1_out_12, and_2_out_10, and_2_out_11, and_2_out_12, and_3_out_10,
       and_3_out_11, and_3_out_12, not_1_out_4, not_1_out_5, not_1_out_6, not_2_out_4, not_2_out_6,
       not_3_out_6;

  \not  not_1 (.in_1(A), .in_3(B), .out_4(not_1_out_4), .out_5(not_1_out_5), .out_6(not_1_out_6));  // open: in_2
  \not  not_2 (.in_1(A), .in_3(C), .out_4(not_2_out_4), .out_6(not_2_out_6));  // open: in_2, out_5
  \not  not_3 (.in_3(C), .out_6(not_3_out_6));  // open: in_1, in_2, out_4, out_5
  \and  and_1 (
    .A(C), .A_2(not_1_out_5), .A_3(not_1_out_6), .C_3(not_1_out_4), .out_10(and_1_out_10),
    .out_11(and_1_out_11), .out_12(and_1_out_12));  // open: B, C, B_2, C_2, B_3
  \and  and_2 (
    .A(B), .C_2(not_2_out_6), .C_3(not_2_out_4), .out_10(and_2_out_10), .out_11(and_2_out_11),
    .out_12(and_2_out_12));  // open: B, C, A_2, B_2, A_3, B_3
  \and  and_3 (
    .A(B), .B_2(A), .B_3(not_3_out_6), .out_10(and_3_out_10), .out_11(and_3_out_11), .out_12(and_3_out_12));  // open: B, C, A_2, C_2, A_3, C_3
  \or  or_1 (
    .in_1(and_3_out_11), .in_2(and_1_out_10), .in_3(and_2_out_10), .in_4(and_1_out_11), .in_5(and_2_out_11),
    .in_6(and_1_out_12), .in_7(and_2_out_12), .in_8(and_3_out_12), .in_9(and_3_out_10), .out_10(out_4));  // open: out_11, out_12
endmodule

module OR (
  input  in_1,
  input  in_2,
  input  in_3,
  input  in_4,
  input  in_5,
  input  in_6,
  input  in_7,
  input  in_8,
  input  in_9,
  output out_10,
  output out_11,
  output out_12
);

  or or_1 (out_10, in_1, in_2, in_3);
  or or_2 (out_11, in_4, in_5, in_6);
  or or_3 (out_12, in_7, in_8, in_9);
endmodule

module NOT (
  input  in_1,
  input  in_2,
  input  in_3,
  output out_4,
  output out_5,
  output out_6
);

  not not_1 (out_4, in_1);
  not not_2 (out_5, in_2);
  not not_3 (out_6, in_3);
endmodule

// IC7071
module \or  (
  input  in_1,
  input  in_2,
  input  in_3,
  input  in_4,
  input  in_5,
  input  in_6,
  input  in_7,
  input  in_8,
  input  in_9,
  output out_10,
  output out_11,
  output out_12
);

  or or_1 (out_10, in_1, in_2, in_3);
  or or_2 (out_11, in_4, in_5, in_6);
  or or_3 (out_12, in_7, in_8, in_9);
endmodule

// IC7072
module \and  (
  input  A,
  input  B,
  input  C,
  input  A_2,
  input  B_2,
  input  C_2,
  input  A_3,
  input  B_3,
  input  C_3,
  output out_10,
  output out_11,
  output out_12
);

  and and_1 (out_10, A, B, C);
  and and_2 (out_11, A_2, B_2, C_2);
  and and_3 (out_12, A_3, B_3, C_3);
endmodule

// IC7073
module \not  (
  input  in_1,
  input  in_2,
  input  in_3,
  output out_4,
  output out_5,
  output out_6
);

  not not_1 (out_4, in_1);
  not not_2 (out_5, in_2);
  not not_3 (out_6, in_3);
endmodule
