// Logisim project Lab4 IC shawon.circ as structural Verilog: 4 circuits, main circuit main
module main (
  input  W,
  input  X,
  input  Y,
  input  Z,
  output A,
  output B,
  output C,
  output D
);

  wire and_gate_1_out_17, and_gate_1_out_19, and_gate_1_out_20, and_gate_2_out_17, and_gate_3_out_17,
       and_gate_3_out_20, and_gate_4_out_20, not_gate_2_out_5, not_gate_2_out_6, not_gate_2_out_7,
       not_gate_2_out_8, not_gate_3_out_5, not_gate_3_out_6, not_gate_4_out_7;

  not_gate not_gate_1 ();  // open: A, B, C, D, out_5, out_6, out_7, out_8
  not_gate not_gate_2 (
    .A(X), .B(X), .C(Y), .D(Z), .out_5(not_gate_2_out_5), .out_6(not_gate_2_out_6), .out_7(not_gate_2_out_7),
    .out_8(not_gate_2_out_8));
  not_gate not_gate_3 (.A(Y), .B(Z), .out_5(not_gate_3_out_5), .out_6(not_gate_3_out_6));  // open: C, D, out_7, out_8
  not_gate not_gate_4 (.C(Z), .out_7(not_gate_4_out_7));  // open: A, B, D, out_5, out_6, out_8
  and_gate and_gate_1 (
    .C(Y), .A_2(not_gate_2_out_5), .C_2(not_gate_2_out_7), .B_3(Z), .D_3(not_gate_2_out_8), .C_4(X),
    .D_4(not_gate_2_out_6), .out_17(and_gate_1_out_17), .out_19(and_gate_1_out_19), .out_20(and_gate_1_out_20));  // open: A, B, D, B_2, D_2, A_3, C_3, A_4, B_4, out_18
  and_gate and_gate_2 (
    .A(not_gate_4_out_7), .out_17(and_gate_2_out_17));  // open: B, C, D, A_2, B_2, C_2, D_2, A_3, B_3, C_3, D_3, A_4, B_4, C_4, D_4, out_18, out_19, out_20
  and_gate and_gate_3 (
    .A(X), .B(Z), .C(X), .C_4(Y), .out_17(and_gate_3_out_17), .out_20(and_gate_3_out_20));  // open: D, A_2, B_2, C_2, D_2, A_3, B_3, C_3, D_3, A_4, B_4, D_4, out_18, out_19
  and_gate and_gate_4 (
    .B(not_gate_3_out_5), .B_2(not_gate_3_out_6), .C_4(Z), .D_4(Y), .out_20(and_gate_4_out_20));  // open: A, C, D, A_2, C_2, D_2, A_3, B_3, C_3, D_3, A_4, B_4, out_17, out_18, out_19
  or_gate or_gate_1 (
    .A(W), .B(and_gate_3_out_17), .C(and_gate_3_out_20), .W(A));  // open: D, A_2, B_2, C_2, D_2, A_3, B_3, C_3, D_3, A_4, B_4, C_4, D_4, X, Y, Z
  or_gate or_gate_2 (
    .A_2(and_gate_1_out_17), .C_2(and_gate_1_out_19), .B_3(and_gate_1_out_20), .Y(B));  // open: A, B, C, D, B_2, D_2, A_3, C_3, D_3, A_4, B_4, C_4, D_4, W, X, Z
  or_gate or_gate_3 (
    .C_3(and_gate_4_out_20), .W(C));  // open: A, B, C, D, A_2, B_2, C_2, D_2, A_3, B_3, D_3, A_4, B_4, C_4, D_4, X, Y, Z
  or_gate or_gate_4 (
    .C_2(and_gate_2_out_17), .Z(D));  // open: A, B, C, D, A_2, B_2, D_2, A_3, B_3, C_3, D_3, A_4, B_4, C_4, D_4, W, X, Y
endmodule

// IC 7066
module and_gate (
  input  A,
  input  B,
  input  C,
  input  D,
  input  A_2,
  input  B_2,
  input  C_2,
  input  D_2,
  input  A_3,
  input  B_3,
  input  C_3,
  input  D_3,
  input  A_4,
  input  B_4,
  input  C_4,
  input  D_4,
  output out_17,
  output out_18,
  output out_19,
  output out_20
);

  and and_1 (out_17, A, B, C, D);
  and and_2 (out_18, A_2, B_2, C_2, D_2);
  and and_3 (out_19, A_3, B_3, C_3, D_3);
  and and_4 (out_20, A_4, B_4, C_4, D_4);
endmodule

// IC 7061
module not_gate (
  input  A,
  input  B,
  input  C,
  input  D,
  output out_5,
  output out_6,
  output out_7,
  output out_8
);

  not not_1 (out_5, A);
  not not_2 (out_6, B);
  not not_3 (out_7, C);
  not not_4 (out_8, D);
endmodule

// IC 7011
module or_gate (
  input  A,
  input  B,
  input  C,
  input  D,
  input  A_2,
  input  B_2,
  input  C_2,
  input  D_2,
  input  A_3,
  input  B_3,
  input  C_3,
  input  D_3,
  input  A_4,
  input  B_4,
  input  C_4,
  input  D_4,
  output W,
  output X,
  output Y,
  output Z
);

  or or_1 (W, A, B, C, D);
  or or_2 (X, A_2, B_2, C_2, D_2);
  or or_3 (Y, A_3, B_3, C_3, D_3);
  or or_4 (Z, A_4, B_4, C_4, D_4);
endmodule
