// Logisim project T.circ as structural Verilog: 1 circuit, main circuit main
module main (
  input  X,
  output [1:0] out_2
);

  wire clock_1_out, xor_1_out;

  xor xor_1 (xor_1_out, X, out_2[1]);
  T_Flip_Flop t_ff_1 (.clk(clock_1_out), .T(xor_1_out), .Q(out_2[0]));  // open: Qn, preset, reset, en
  T_Flip_Flop t_ff_2 (.clk(clock_1_out), .T(1'b1), .Q(out_2[1]));  // open: Qn, preset, reset, en
  Clock clock_1 (.out(clock_1_out));
endmodule
