// Logisim project lab-5 Ic 3.circ as structural Verilog: 5 circuits, main circuit main
module main (
  input  B4,
  input  B3,
  input  B2,
  input  B1,
  input  M,
  input  A4,
  input  A3,
  input  A2,
  input  A1,
  input  B4_2,
  input  B3_2,
  input  B2_2,
  input  B1_2,
  input  M_2,
  input  A1_2,
  input  A2_2,
  input  A3_2,
  input  A4_2,
  output C,
  output out_20,
  output S4,
  output S3,
  output S2,
  output S1
);

  wire and_1_out, and_2_out, n4_bit_binary_adder_1_cout, n4_bit_binary_adder_1_s1, n4_bit_binary_adder_1_s2,
       n4_bit_binary_adder_1_s3, n4_bit_binary_adder_1_s4, or_1_out;

  _4_bit_binary_adder u_4_bit_binary_adder_1 (
    .Cin(B2), .A1(A1), .B1(B1), .A2(A2), .B2(B2), .A3(A3), .B3(B3), .A4(A4), .B4(B4),
    .S1(n4_bit_binary_adder_1_s1), .S2(n4_bit_binary_adder_1_s2), .S3(n4_bit_binary_adder_1_s3),
    .S4(n4_bit_binary_adder_1_s4), .Cout(n4_bit_binary_adder_1_cout));
  _4_bit_binary_adder u_4_bit_binary_adder_2 (
    .Cin(B4_2), .A1(A4_2), .B1(B1_2), .A2(A3_2), .B2(B2_2), .A3(A2_2), .B3(B3_2), .A4(A1_2), .B4(B4_2),
    .S1(S1), .S2(S2), .S3(S3), .S4(S4), .Cout(out_20));
  and and_1 (and_1_out, n4_bit_binary_adder_1_s4, n4_bit_binary_adder_1_s3);
  and and_2 (and_2_out, n4_bit_binary_adder_1_s4, n4_bit_binary_adder_1_s2);
  or or_1 (or_1_out, and_1_out, and_2_out);
  or or_2 (A2_2, n4_bit_binary_adder_1_cout, or_1_out);

  assign C = A2_2;
  assign M = B2;
  assign M_2 = B4_2;
endmodule

module OR_gates (
  input  in_1,
  input  in_2,
  input  in_3,
  input  in_4,
  input  in_5,
  input  in_6,
  input  in_7,
  input  in_8,
  output out_9,
  output out_10,
  output out_11,
  output out_12
);

  or or_1 (out_9, in_1, in_2);
  or or_2 (out_10, in_3, in_4);
  or or_3 (out_11, in_5, in_6);
  or or_4 (out_12, in_7, in_8);
endmodule

module AND_gates (
  input  in_1,
  input  in_2,
  input  in_3,
  input  in_4,
  input  in_5,
  input  in_6,
  input  in_7,
  input  in_8,
  output out_9,
  output out_10,
  output out_11,
  output out_12
);

  and and_1 (out_9, in_1, in_2);
  and and_2 (out_10, in_3, in_4);
  and and_3 (out_11, in_5, in_6);
  and and_4 (out_12, in_7, in_8);
endmodule

module XOR_gates (
  input  in_1,
  input  in_2,
  input  in_3,
  input  in_4,
  input  in_5,
  input  in_6,
  input  in_7,
  input  in_8,
  output out_9,
  output out_10,
  output out_11,
  output out_12
);

  xor xor_1 (out_9, in_1, in_2);
  xor xor_2 (out_10, in_3, in_4);
  xor xor_3 (out_11, in_5, in_6);
  xor xor_4 (out_12, in_7, in_8);
endmodule

// IC 74283
module _4_bit_binary_adder (
  input  Cin,
  input  A1,
  input  B1,
  input  A2,
  input  B2,
  input  A3,
  input  B3,
  input  A4,
  input  B4,
  output S1,
  output S2,
  output S3,
  output S4,
  output Cout
);

  wire adder_1_cout, adder_2_cout, adder_3_cout;

  Adder #(.width(1)) adder_1 (.a(A1), .b(B1), .out(S1), .cin(Cin), .cout(adder_1_cout));
  Adder #(.width(1)) adder_2 (.a(A2), .b(B2), .out(S2), .cin(adder_1_cout), .cout(adder_2_cout));
  Adder #(.width(1)) adder_3 (.a(A3), .b(B3), .out(S3), .cin(adder_2_cout), .cout(adder_3_cout));
  Adder #(.width(1)) adder_4 (.a(A4), .b(B4), .out(S4), .cin(adder_3_cout), .cout(Cout));
endmodule
