// Logisim project lab-5 Ic.circ as structural Verilog: 5 circuits, main circuit main
module main (
  input  A4,
  input  A3,
  input  A2,
  input  A1,
  input  B4,
  input  B3,
  input  B2,
  input  B1,
  input  M,
  output Cout,
  output S4,
  output S3,
  output S2,
  output S1
);

  wire xor_1_out, xor_2_out, xor_3_out, xor_4_out;

  xor xor_1 (xor_1_out, B4, M);
  buf xor_2 (xor_2_out, B3);  // XOR_Gate
  buf xor_3 (xor_3_out, B2);  // XOR_Gate
  buf xor_4 (xor_4_out, B1);  // XOR_Gate
  _4_bit_binary_adder u_4_bit_binary_adder_1 (
    .Cin(M), .A1(A4), .B1(xor_1_out), .A2(A3), .B2(xor_2_out), .A3(A2), .B3(xor_3_out), .A4(A1),
    .B4(xor_4_out), .S1(S4), .S2(S3), .S3(S2), .S4(S1), .Cout(Cout));
endmodule

module OR_gates (
  input  in_1,
  input  in_2,
  input  in_3,
  input  in_4,
  input  in_5,
  input  in_6,
  input  in_7,
  input  in_8,
  output out_9,
  output out_10,
  output out_11,
  output out_12
);

  or or_1 (out_9, in_1, in_2);
  or or_2 (out_10, in_3, in_4);
  or or_3 (out_11, in_5, in_6);
  or or_4 (out_12, in_7, in_8);
endmodule

module AND_gates (
  input  in_1,
  input  in_2,
  input  in_3,
  input  in_4,
  input  in_5,
  input  in_6,
  input  in_7,
  input  in_8,
  output out_9,
  output out_10,
  output out_11,
  output out_12
);

  and and_1 (out_9, in_1, in_2);
  and and_2 (out_10, in_3, in_4);
  and and_3 (out_11, in_5, in_6);
  and and_4 (out_12, in_7, in_8);
endmodule

module XOR_gates (
  input  in_1,
  input  in_2,
  input  in_3,
  input  in_4,
  input  in_5,
  input  in_6,
  input  in_7,
  input  in_8,
  output out_9,
  output out_10,
  output out_11,
  output out_12
);

  xor xor_1 (out_9, in_1, in_2);
  xor xor_2 (out_10, in_3, in_4);
  xor xor_3 (out_11, in_5, in_6);
  xor xor_4 (out_12, in_7, in_8);
endmodule

// IC 74283
module _4_bit_binary_adder (
  input  Cin,
  input  A1,
  input  B1,
  input  A2,
  input  B2,
  input  A3,
  input  B3,
  input  A4,
  input  B4,
  output S1,
  output S2,
  output S3,
  output S4,
  output Cout
);

  wire adder_1_cout, adder_2_cout, adder_3_cout;

  Adder #(.width(1)) adder_1 (.a(A1), .b(B1), .out(S1), .cin(Cin), .cout(adder_1_cout));
  Adder #(.width(1)) adder_2 (.a(A2), .b(B2), .out(S2), .cin(adder_1_cout), .cout(adder_2_cout));
  Adder #(.width(1)) adder_3 (.a(A3), .b(B3), .out(S3), .cin(adder_2_cout), .cout(adder_3_cout));
  Adder #(.width(1)) adder_4 (.a(A4), .b(B4), .out(S4), .cin(adder_3_cout), .cout(Cout));
endmodule
